// Digital circuit BW8cpu.dig as structural Verilog
module BW8cpu (
  input  step,
  input  crystal,
  input  _555,
  output pass,
  output fail
);

  wire a_dbus_a, a_dbus_l, a_lhs_a, a_rhs_a, ack_addr_a, addr_inc, addr_xfer_a, alu_dbus_a, alu_res,
       b_dbus_a, b_dbus_l, b_lhs_a, b_rhs_a, c_dbus_a, c_dbus_l, c_lhs_a, c_rhs_a, clk, clk_crystal,
       comparator_1_eq, d_dbus_a, d_dbus_l, d_lhs_a, d_rhs_a, da_dbus_a, da_dbus_l, dec_sp, dp_dbus_a,
       dp_dbus_l, ext, ir_dbus_l, lsb_dbus_a, mem_dbus_a, mem_dbus_l, msb_dbus_a, nclk, noffset, not_1_out,
       not_2_out, not_3_out, not_4_out, not_5_out, nrst, nRST_out, off_dbus_l, pc_addr_a, pc_inc, pc_xfer_a,
       pc_xfer_l, pch_dbus_l, pcl_dbus_l, pulldown_5_out, reg_a, reg_b, reg_c, reg_d, reg_da, reg_dp,
       reset_1_out, rst, sp_addr_a, sp_inc, sp_xfer_a, sp_xfer_l, sph_dbus_l, spl_dbus_l, sr_dbus_a,
       sr_dbus_l, t_addr_a, th_dbus_a, th_dbus_l, th_lhs_a, tl_dbus_a, tl_dbus_l, tl_rhs_a, undriven,
       x_addr_a, x_inc, x_xfer_a, x_xfer_l, xh_dbus_l, xl_dbus_l, y_addr_a, y_inc, y_xfer_a, y_xfer_l,
       yh_dbus_l, yl_dbus_l;
  wire [2:0] addr_a, Break_out, clk_mode, count, t_state, xfer_l;
  wire [3:0] alu_op, dbus_a;
  wire [4:0] dbus_l, flags, xfer_a;
  wire [7:0] dbus, driver_1_out, driver_2_out, lhs, mbus, opcode, reg_off, reg_th, reg_tl, rhs;
  wire [15:0] addr, addr_out, reg_pc, reg_sp, reg_x, reg_y;
  wire [17:3] Control_Unit_dbg;

  PullDown #(.Bits(8)) pulldown_1 (.out(dbus));
  PullDown #(.Bits(16)) pulldown_2 (.out({lhs, rhs}));
  // Probe on dbus
  // Probe on {lhs, rhs}
  // Probe on reg_a
  // Probe on reg_b
  // Probe on reg_c
  // Probe on reg_d
  // Probe on reg_dp
  // Probe on reg_da
  // Probe on reg_tl
  // Probe on reg_th
  // Probe C_f on flags[4]
  // Probe Z_f on flags[3]
  LED led_1 (.in(clk));
  // Probe on addr
  // Probe on mbus
  // Probe on reg_pc
  // Probe on reg_sp
  // Probe on reg_x
  // Probe on reg_y
  // Probe on addr_out
  // Probe on reg_off
  // Probe on alu_res
  // Probe N_f on flags[1]
  // Probe V_f on flags[2]
  // Probe I_f on flags[0]
  PullDown #(.Bits(16)) pulldown_3 (.out(addr));
  PullDown #(.Bits(8)) pulldown_4 (.out(mbus));
  // Probe on opcode
  // Probe on ext
  Reset reset_1 (.out(reset_1_out));
  Button #(.activeLow("true")) u_nRST (.out(nRST_out));
  Button #(.activeLow("true")) Run (.out(Break_out[0]));
  Button #(.activeLow("true")) Demo (.out(Break_out[1]));
  Button #(.activeLow("true")) Break (.out(Break_out[2]));
  // Probe on flags
  control_unit Control_Unit (
    .nirq(1'b1), .opcode(opcode), .flags(flags), .nreq(1'b1), .nrst(nrst), .nnmi(pulldown_5_out),
    .NMI_Inhib(1'b1), .clk(clk), .dbus_assert(dbus_a), .dbus_load(dbus_l), .alu_op(alu_op),
    .xfer_assert(xfer_a), .xfer_load(xfer_l), .addr_assert(addr_a), .count(count), .dec_sp(dec_sp),
    .nclk(nclk), .noffset(noffset), .rst(rst),
    .dbg({Control_Unit_dbg[17:16], ext, Control_Unit_dbg[14:3], t_state}));
  PullDown pulldown_5 (.out(pulldown_5_out));
  instruction_register Instruction_Register (
    .dbus(dbus), .ndbus_load(ir_dbus_l), .clr(rst), .nclk(nclk), .opcode(opcode));
  memory_bridge Memory_Bridge (.dbus_assert(mem_dbus_a), .dbus_load(mem_dbus_l), .dbus(dbus), .mbus(mbus));
  ROM #(.AddrBits(16), .isProgramMemory("true"), .Bits(8)) ROM (.A(addr_out), .sel(1'b1), .D(mbus));
  and and_1 (nrst, reset_1_out, nRST_out);
  // Probe on t_state
  // triple_clock triple_clock_1: pin names not known; wires that end beside it: Break_out, 1'b1, {nrst, 2'b11}, crystal, _555, step, clk, clk_crystal, clk_mode
  // Probe on nclk
  LED Run_Mode_Active (.in(clk_mode[0]));
  LED Demo_Mode_Active (.in(clk_mode[1]));
  LED Break_Mode_Active (.in(clk_mode[2]));
  // Probe on count
  // Probe on dec_sp
  LED cpu (.in(clk));
  LED u_crystal (.in(clk_crystal));
  // Probe on addr_a
  // Probe on xfer_l
  // Probe on xfer_a
  // bus_controller Bus_Controller: pin names not known; wires that end beside it: dbus_a, xfer_l, addr_a, clk, count, dec_sp, nclk, dbus_l, xfer_a, alu_dbus_a, a_dbus_a, b_dbus_a, c_dbus_a, d_dbus_a, dp_dbus_a, da_dbus_a, th_dbus_a, tl_dbus_a, sr_dbus_a, mem_dbus_a, msb_dbus_a, lsb_dbus_a, a_dbus_l, b_dbus_l, c_dbus_l
  // Probe on alu_op
  // Probe on dbus_l
  // Probe on dbus_a
  not not_1 (not_1_out, undriven);
  assign driver_1_out = not_1_out ? dbus : 8'bz;  // Driver driver_1
  assign driver_2_out = not_1_out ? lhs : 8'bz;  // Driver driver_2
  PullDown #(.Bits(8)) pulldown_6 (.out(driver_2_out));
  Comparator #(.Bits(8)) comparator_1 (.a(driver_1_out), .b(driver_2_out), .eq(comparator_1_eq));  // open: gt, lt
  not not_2 (not_2_out, undriven);
  PullDown #(.Bits(8)) pulldown_7 (.out(driver_1_out));
  // alu Arithmetic___Logic_Unit_and_Status_Register: pin names not known; wires that end beside it: alu_op, sr_dbus_l, sr_dbus_a, nclk, rst, lhs, rhs, alu_dbus_a, flags, dbus, alu_res
  // gpr_pair A_and_B: pin names not known; wires that end beside it: a_dbus_l, b_dbus_l, a_dbus_a, b_dbus_a, a_lhs_a, b_lhs_a, a_rhs_a, b_rhs_a, dbus, rst, nclk, reg_a, reg_b, {lhs, rhs}
  // gpr_pair C_and_D: pin names not known; wires that end beside it: mem_dbus_l, ir_dbus_l, off_dbus_l, pch_dbus_l, pcl_dbus_l, sph_dbus_l, spl_dbus_l, xh_dbus_l, xl_dbus_l, c_dbus_l, d_dbus_l, c_dbus_a, d_dbus_a, c_lhs_a, d_lhs_a, c_rhs_a, d_rhs_a, dbus, rst, nclk, reg_c, reg_d, {lhs, rhs}
  // gpr_pair DA_and_DP: pin names not known; wires that end beside it: addr_xfer_a, a_lhs_a, b_lhs_a, c_lhs_a, d_lhs_a, th_lhs_a, a_rhs_a, b_rhs_a, c_rhs_a, dp_dbus_l, da_dbus_l, dp_dbus_a, da_dbus_a, 1'b1, 1'b1, 1'b1, 1'b1, dbus, rst, nclk, reg_dp, reg_da, {lhs, rhs}
  temp_reg_pair temp_reg_pair_1 (
    .nhi_dbus_load(th_dbus_l), .nlo_dbus_load(tl_dbus_l), .nhi_dbus_assert(th_dbus_a),
    .nlo_dbus_assert(tl_dbus_a), .nhi_lhs_assert(th_lhs_a), .nlo_lhs_assert(1'b1), .nhi_rhs_assert(1'b1),
    .nlo_rhs_assert(tl_rhs_a), .dbus(dbus), .clr(rst), .nclk(nclk), .naddr_assert(t_addr_a), .reg_hi(reg_th),
    .reg_lo(reg_tl), .xfer({lhs, rhs}), .addr(addr));
  not not_3 (not_3_out, comparator_1_eq);
  and and_2 (pass, comparator_1_eq, not_2_out);
  and and_3 (fail, not_2_out, not_3_out);
  not not_4 (not_4_out, addr_inc);
  not not_5 (not_5_out, ack_addr_a);
  address_register Program_Counter (
    .clk(clk), .clr(rst), .inc(pc_inc), .dec(1'b1), .xfer_load(pc_xfer_l), .addr_assert(pc_addr_a),
    .xfer_assert(pc_xfer_a), .dbus_load_hi(pch_dbus_l), .dbus_load_lo(pcl_dbus_l), .dbus(dbus), .addr(addr),
    .xfer({lhs, rhs}), .\reg (reg_pc));
  address_register Stack_Pointer (
    .clk(clk), .clr(rst), .inc(sp_inc), .dec(1'b1), .xfer_load(sp_xfer_l), .addr_assert(sp_addr_a),
    .xfer_assert(sp_xfer_a), .dbus_load_hi(sph_dbus_l), .dbus_load_lo(spl_dbus_l), .dbus(dbus), .addr(addr),
    .xfer({lhs, rhs}), .\reg (reg_sp));
  address_register X_Index (
    .clk(clk), .clr(rst), .inc(x_inc), .dec(1'b1), .xfer_load(x_xfer_l), .addr_assert(x_addr_a),
    .xfer_assert(x_xfer_a), .dbus_load_hi(xh_dbus_l), .dbus_load_lo(xl_dbus_l), .dbus(dbus), .addr(addr),
    .xfer({lhs, rhs}), .\reg (reg_x));
  address_register Y_Index (
    .clk(clk), .clr(rst), .inc(y_inc), .dec(1'b1), .xfer_load(y_xfer_l), .addr_assert(y_addr_a),
    .xfer_assert(y_xfer_a), .dbus_load_hi(yh_dbus_l), .dbus_load_lo(yl_dbus_l), .dbus(dbus), .addr(addr),
    .xfer({lhs, rhs}), .\reg (reg_y));
  address_offset Address_Bridge (
    .nclk(off_dbus_l), .dbus(dbus), .addr_in(addr), .noffset_en(noffset), .carry_en(not_4_out),
    .naddr_xfer_assert(addr_xfer_a), .nassert_addr(not_5_out), .nclr(nrst), .addr_out(addr_out),
    .xfer({lhs, rhs}), .q(reg_off));

  // Other names for the same wires on the sheet: clk_cpu = clk; rst_clk_mode[2] = nrst; xfer[15:0] = {lhs, rhs}

  // Notes on the sheet:
  //   crystal: Hz: 5
  //   External Pinout
  //   Buses & Constants
  //   Registers
  //   ROM loads sim_test.bin
endmodule
