// Digital circuit control_unit.dig as structural Verilog
module control_unit (
  input  nirq,
  input  [7:0] opcode,
  input  [4:0] flags,
  input  nreq,
  input  clk,
  input  nrst,
  output [3:0] dbus_assert,
  output [3:0] dbus_load,
  output [4:0] alu_op,
  output [4:0] xfer_assert,
  output [2:0] xfer_load,
  output [2:0] addr_assert,
  output [2:0] count,
  output dec_sp,
  output nbrk,
  output nclk,
  output rst
);

  wire clk_inverter_p3, clk_inverter_p4, clk_inverter_p5, clk_inverter_p6, rst_useq, sequencer_p1,
       sequencer_p4, sequencer_p5, sequencer_p6;
  wire [1:0] m_tog;
  wire [2:0] t_state;
  wire [7:0] ucode0_d, ucode1_d, ucode2_d, ucode3_d;
  wire [7:1] Latch_IRQ_q;
  wire [16:16] ucode_addr;

  // _7404 clk_inverter: pin names not known; wires that end beside it: clk, nrst, clk_inverter_p3, clk_inverter_p4, clk_inverter_p5, clk_inverter_p6, 1'b1, 1'b0, nclk, rst
  // NotConnected on clk_inverter_p3
  // NotConnected on clk_inverter_p4
  // NotConnected on clk_inverter_p5
  // NotConnected on clk_inverter_p6
  _74ls574 Latch_IRQ (
    .nOC(1'b0), .CLK(clk), .D({7'b0000001, nirq}), .VCC(1'b1), .GND(1'b0), .Q({Latch_IRQ_q, ucode_addr[16]}));
  // _74193 sequencer: pin names not known; wires that end beside it: sequencer_p1, 1'b1, clk, sequencer_p4, sequencer_p5, sequencer_p6, rst_useq, 1'b1, 1'b1, 1'b0, t_state[0], t_state[1], t_state[2]
  // NotConnected on sequencer_p1
  // NotConnected on sequencer_p4
  // NotConnected on sequencer_p5
  // NotConnected on sequencer_p6
  ROM #(.AddrBits(19), .Bits(8)) ucode0 (.A({2'b11, ucode_addr[16], opcode, flags, t_state}), .sel(1'b1), .D(ucode0_d));
  ROM #(.AddrBits(19), .Bits(8)) ucode1 (.A({2'b11, ucode_addr[16], opcode, flags, t_state}), .sel(1'b1), .D(ucode1_d));
  ROM #(.AddrBits(19), .Bits(8)) ucode2 (.A({2'b11, ucode_addr[16], opcode, flags, t_state}), .sel(1'b1), .D(ucode2_d));
  ROM #(.AddrBits(19), .Bits(8)) ucode3 (.A({2'b11, ucode_addr[16], opcode, flags, t_state}), .sel(1'b1), .D(ucode3_d));
  _74ls574 _74ls574_1 (.nOC(rst), .CLK(nclk), .D(ucode0_d), .VCC(1'b1), .GND(1'b0), .Q({dbus_load, dbus_assert}));
  _74ls574 _74ls574_2 (.nOC(rst), .CLK(nclk), .D(ucode1_d), .VCC(1'b1), .GND(1'b0), .Q({xfer_assert[2:0], alu_op}));
  _74ls574 _74ls574_3 (
    .nOC(rst), .CLK(nclk), .D(ucode2_d), .VCC(1'b1), .GND(1'b0),
    .Q({addr_assert, xfer_load, xfer_assert[4:3]}));
  _74ls574 _74ls574_4 (
    .nOC(rst), .CLK(nclk), .D(ucode3_d), .VCC(1'b1), .GND(1'b0), .Q({nbrk, m_tog, rst_useq, dec_sp, count}));
  _74ls245 _74ls245_1 (.DIR(1'b1), .nOE(nrst), .A({8{1'b0}}), .B({dbus_load, dbus_assert}), .VCC(1'b1), .GND(1'b0));
  _74ls245 _74ls245_2 (.DIR(1'b1), .nOE(nrst), .A({8{1'b0}}), .B({xfer_assert[2:0], alu_op}), .VCC(1'b1), .GND(1'b0));
  _74ls245 _74ls245_3 (
    .DIR(1'b1), .nOE(nrst), .A({8{1'b0}}), .B({addr_assert, xfer_load, xfer_assert[4:3]}), .VCC(1'b1),
    .GND(1'b0));
  _74ls245 _74ls245_4 (
    .DIR(1'b1), .nOE(nrst), .A(8'h90), .B({nbrk, m_tog, rst_useq, dec_sp, count}), .VCC(1'b1), .GND(1'b0));

  // Other names for the same wires on the sheet: xa_3 = xfer_assert[3]; xa_4 = xfer_assert[4]; xa_0 = xfer_assert[0];
  //   xa_1 = xfer_assert[1]; xa_2 = xfer_assert[2]; ucode_addr[15:0] = {opcode, flags, t_state}

  // Notes on the sheet:
  //   ucode0 loads control_0.bin
  //   ucode1 loads control_1.bin
  //   ucode2 loads control_2.bin
  //   ucode3 loads control_3.bin
endmodule
